# Fritzing sketch esquema para cada tubo (doble cobre)MOSFET-V2 (saved by Fritzing 0.8.0b)

parts:
  U4 = mystery part, 5 pins [chip_label=?]
  U1 = 74HC595 [package="DIP16 [THT]"]
  C1 = Ceramic Capacitor [capacitance=100nF package="100 mil [THT, multilayer]"]
  U3 = 74HC595 [package="DIP16 [THT]"]
  U2 = 74HC595 [package="DIP16 [THT]"]
  U5 = mystery part, 3 pins [chip_label=?]  # not connected
  U6 = mystery part, 3 pins [chip_label=?]  # not connected
  U7 = mystery part, 3 pins [chip_label=?]  # not connected
  U9 = mystery part, 3 pins [chip_label=?]  # not connected
  U10 = mystery part, 3 pins [chip_label=?]  # not connected
  U11 = mystery part, 3 pins [chip_label=?]  # not connected
  U12 = mystery part, 3 pins [chip_label=?]  # not connected
  Q1 = NPN-Transistor [package="SOT-23 [SMD]"]  # not connected
  Q2 = NPN-Transistor [package="SOT-23 [SMD]"]  # not connected
  Q3 = NPN-Transistor [package="SOT-23 [SMD]"]  # not connected
  Q4 = NPN-Transistor [package="SOT-23 [SMD]"]  # not connected
  Q5 = NPN-Transistor [package="SOT-23 [SMD]"]  # not connected
  Q6 = NPN-Transistor [package="SOT-23 [SMD]"]  # not connected
  Q7 = NPN-Transistor [package="SOT-23 [SMD]"]  # not connected
  Q8 = NPN-Transistor [package="SOT-23 [SMD]"]  # not connected
  Q9 = NPN-Transistor [package="SOT-23 [SMD]"]  # not connected
  Q10 = NPN-Transistor [package="SOT-23 [SMD]"]  # not connected
  Q11 = NPN-Transistor [package="SOT-23 [SMD]"]  # not connected
  Q12 = NPN-Transistor [package="SOT-23 [SMD]"]  # not connected
  Q13 = NPN-Transistor [package="SOT-23 [SMD]"]  # not connected
  Q14 = NPN-Transistor [package="SOT-23 [SMD]"]  # not connected
  Q15 = NPN-Transistor [package="SOT-23 [SMD]"]  # not connected
  Q16 = NPN-Transistor [package="SOT-23 [SMD]"]  # not connected
  Q17 = NPN-Transistor [package="SOT-23 [SMD]"]  # not connected
  Q18 = NPN-Transistor [package="SOT-23 [SMD]"]  # not connected
  Q19 = NPN-Transistor [package="SOT-23 [SMD]"]  # not connected
  Q20 = NPN-Transistor [package="SOT-23 [SMD]"]  # not connected
  Q21 = NPN-Transistor [package="SOT-23 [SMD]"]  # not connected
  Q22 = NPN-Transistor [package="SOT-23 [SMD]"]  # not connected
  Q23 = NPN-Transistor [package="SOT-23 [SMD]"]  # not connected
  Q24 = NPN-Transistor [package="SOT-23 [SMD]"]  # not connected
  U8 = mystery part, 3 pins [chip_label=?]  # not connected

nets:
  VCC: U4.pin1, U1.MR, U1.VCC, U3.MR, U3.VCC, U2.MR, U2.VCC
  N1: U4.pin2, U2.DS
  GND: U4.pin3, U1.GND, U1.OE, C1.0, U3.GND, U3.OE, U2.GND, U2.OE
  N2: U4.pin4, U1.ST_CP, C1.1, U3.ST_CP, U2.ST_CP
  N3: U4.pin5, U1.SH_CP, U3.SH_CP, U2.SH_CP
  N4: U1.DS, U3.Q7'
  N5: U3.DS, U2.Q7'

notes:
  GND
  c
  L
  C
  +
  -
  D
  v
  1
  2
  3
  4
  5
  6
  7
  8
